// Logisim project labb_4_assigment_1.circ as structural Verilog: 2 circuits, main circuit main
module main (
  input  [31:0] A,
  input  [31:0] B,
  input  [2:0] F,
  output [31:0] Y,
  output Zero
);

  wire comparator_1_gt;
  wire [31:0] adder_1_out, and_1_out, bit_extender_1_out, or_1_out, subtractor_1_out;

  Adder #(.width(32)) adder_1 (.a(A), .b(B), .out(adder_1_out));  // open: cin, cout
  Subtractor #(.width(32)) subtractor_1 (.a(A), .b(B), .out(subtractor_1_out));  // open: bin, bout
  assign and_1_out = A & B;  // AND_Gate and_1, 32 bits wide
  assign or_1_out = A | B;  // OR_Gate or_1, 32 bits wide
  Comparator #(.width(32)) comparator_1 (.a(A), .b(B), .gt(comparator_1_gt));  // open: eq, lt
  ALU alu_1 ();  // open: A, B, F, Y, Zero
  Multiplexer #(.select(3), .width(32)) multiplexer_1 (
    .in0(adder_1_out), .in1(subtractor_1_out), .in2(and_1_out), .in3(or_1_out), .in5(bit_extender_1_out),
    .out(Y), .sel(F));  // open: in4, in6, in7
  assign bit_extender_1_out = {{31{1'b0}}, comparator_1_gt};  // Bit_Extender bit_extender_1
  Comparator #(.width(32)) comparator_2 (.a(Y), .b({32{1'b0}}), .eq(Zero));  // open: gt, lt
endmodule

module ALU (
  input  [31:0] A,
  input  [31:0] B,
  input  [2:0] F,
  output [31:0] Y,
  output Zero
);

  wire comparator_1_gt;
  wire [31:0] adder_1_out, and_1_out, bit_extender_1_out, or_1_out, subtractor_1_out;

  Adder #(.width(32)) adder_1 (.a(A), .b(B), .out(adder_1_out));  // open: cin, cout
  Subtractor #(.width(32)) subtractor_1 (.a(A), .b(B), .out(subtractor_1_out));  // open: bin, bout
  assign and_1_out = A & B;  // AND_Gate and_1, 32 bits wide
  assign or_1_out = A | B;  // OR_Gate or_1, 32 bits wide
  Comparator #(.width(32)) comparator_1 (.a(A), .b(B), .gt(comparator_1_gt));  // open: eq, lt
  Multiplexer #(.select(3), .width(32)) multiplexer_1 (
    .in0(adder_1_out), .in1(subtractor_1_out), .in2(and_1_out), .in3(or_1_out), .in5(bit_extender_1_out),
    .out(Y), .sel(F));  // open: in4, in6, in7
  assign bit_extender_1_out = {{31{1'b0}}, comparator_1_gt};  // Bit_Extender bit_extender_1
  Comparator #(.width(32)) comparator_2 (.a(Y), .b({32{1'b0}}), .eq(Zero));  // open: gt, lt
endmodule
